// Logisim project binarycomparison.circ as structural Verilog
module main (
  input  in_1,
  input  in_2,
  input  in_3,
  input  in_4,
  input  in_5,
  input  in_6,
  output out_7
);

  bincomparison bincomparison_1 (.A1(in_1), .B1(in_2), .C1(in_3), .A2(in_4), .B2(in_5), .C2(in_6), .OFINAL(out_7));
endmodule

// VHDL entity bincomparison, as the project stores it:
--------------------------------------------------------------------------------
-- Project : 
-- File    :
-- Autor   : Gabriel 
-- Date    : 28/07/2021
--
--------------------------------------------------------------------------------
-- Description : This circuit/VHDL compares two binary number of 3-bits
--
--------------------------------------------------------------------------------

LIBRARY ieee;
USE ieee.std_logic_1164.all;

ENTITY bincomparison IS
  PORT (
  ------------------------------------------------------------------------------
    A1 		: IN  std_logic;
    B1 		: IN  std_logic;
    C1 		: IN  std_logic;
    
    A2 		: IN  std_logic;
    B2 		: IN  std_logic;
    C2 		: IN  std_logic;

    OFINAL	: OUT STD_LOGIC
    );
END bincomparison;

--------------------------------------------------------------------------------
--------------------------------------------------------------------------------

ARCHITECTURE TypeArchitecture OF bincomparison IS

BEGIN

	OFINAL <= (A1 XNOR A2) AND (B1 XNOR B2) AND (C1 XNOR C2);



	
END TypeArchitecture;
